# Fritzing sketch weatherlox-air-pcb (saved by Fritzing 1.0.6)
circuit board: 2.5cm x 3cm

parts:
  BME280 = GY-BMP280 Breakout
  3_4 = screw terminal, 2 pins [mn=Air]
  1_2 = screw terminal, 2 pins [mn=Air]
  SDA_SCL = screw terminal, 2 pins [mn=I2C]
  +_- = screw terminal, 2 pins [mn=3.3V]

nets:
  N1: BME280.Pin_1, 1_2.pin2, +_-.pin2
  N2: BME280.Pin_2, 1_2.pin1, +_-.pin1
  N3: BME280.Pin_3, 3_4.pin1, SDA_SCL.pin1
  N4: BME280.Pin_4, 3_4.pin2, SDA_SCL.pin2

notes:
  (c) Michael Schlenstedt
  Version 1.01
  WeatherLox
  Air
  I2C
  3.3V
