# Fritzing sketch weatherlox-esp-pcb (saved by Fritzing 1.0.6)
circuit board: 10cm x 4cm

parts:
  R1 = Resistor [tolerance=±5% resistance=10k power=0.25W package=THT]
  R6 = Resistor [tolerance=±5% resistance=2.2k power=0.25W package=THT]
  R7 = Resistor [tolerance=±5% resistance=2.2k power=0.25W package=THT]
  R4 = Resistor [tolerance=±5% resistance=1.5k power=0.25W package=THT]
  R5 = Resistor [tolerance=±5% resistance=1.5k power=0.25W package=THT]
  R2 = Resistor [tolerance=±5% resistance=10k power=0.25W package=THT]
  5_6_7 = screw terminal, 3 pins [mn=Light]
  1_2 = screw terminal, 2 pins [mn=Air]
  3_4 = screw terminal, 2 pins [mn=Air]
  3_4_2 = screw terminal, 2 pins [mn=Light]
  3_4_3 = screw terminal, 2 pins [mn=WindS]
  1_2_2 = screw terminal, 2 pins [mn=RainA]
  1_2_3 = screw terminal, 3 pins [mn=RainS]
  GND = screw terminal, 2 pins
  +12V = screw terminal, 2 pins
  1_2_3 = screw terminal, 2 pins [mn=Light]
  1_2_4 = screw terminal, 2 pins [mn=WindS]
  1_2_5 = screw terminal, 2 pins [mn=WindD]
  3_4_4 = screw terminal, 2 pins [mn=WindD]
  +_-_D = screw terminal, 3 pins [mn=1-Wire]
  R3 = Resistor [tolerance=±5% resistance=4.7k power=0.25W package=THT]
  +_- = screw terminal, 2 pins [mn=3.3V]
  +_-_2 = screw terminal, 2 pins [mn=Heat]
  COM_ON = screw terminal, 2 pins [mn=Relais]
  +_-_I = screw terminal, 3 pins [mn=Relais]
  U1 = SBX DSUN [package=THT]
  A1 = ESP32 DevKitc V4
  Bauteil1 = Adafruit ADS1115 16Bit I2C ADC [part_number="Adafruit #1085"]
  SDA_SCL = screw terminal, 2 pins

nets:
  N1: R1.Pin_0, 1_2_2.pin1, A1.Pin_11
  GND: R1.Pin_1, R6.Pin_0, R7.Pin_0, 1_2.pin1, 3_4_3.pin2, 1_2_3.pin2, GND.pin1, GND.pin2, 1_2_3.pin1, 1_2_4.pin1, 1_2_5.pin1, 3_4_4.pin2, +_-_D.pin2, +_-.pin1, +_-_2.pin1, +_-_I.pin2, U1.GND, A1.Pin_14, A1.Pin_32, Bauteil1.GND
  N2: R6.Pin_1, R5.Pin_1, Bauteil1.AIN2
  N3: R7.Pin_1, R4.Pin_1, Bauteil1.AIN3
  N4: R4.Pin_0, 3_4_4.pin1
  N5: R5.Pin_0, 3_4_3.pin1
  N6: R2.Pin_0, 1_2_3.pin1, A1.Pin_9
  N7: R2.Pin_1, 1_2.pin2, 1_2_2.pin2, 1_2_3.pin2, +_-_D.pin3, R3.Pin_0, +_-.pin2, A1.Pin_1, Bauteil1.VDD
  N8: 5_6_7.pin1, A1.Pin_8
  N9: 5_6_7.pin2, Bauteil1.AIN1
  N10: 5_6_7.pin3, Bauteil1.AIN0
  N11: 3_4.pin1, 3_4_2.pin1, A1.Pin_36, Bauteil1.SCL, SDA_SCL.pin1
  N12: 3_4.pin2, 3_4_2.pin2, A1.Pin_33, Bauteil1.SDA, SDA_SCL.pin2
  N13: 1_2_3.pin3, +12V.pin1, +12V.pin2, 1_2_4.pin2, 1_2_5.pin2, COM_ON.pin2, U1.+VIN
  N14: +_-_D.pin1, R3.Pin_1, A1.Pin_31
  N15: +_-_2.pin2, COM_ON.pin1
  N16: +_-_I.pin1, A1.Pin_30
  N17: +_-_I.pin3, U1.+VOUT, A1.Pin_19

notes:
  Version 1.01
  (c) Michael Schlenstedt
  WeatherLox
  Relais
  Air
  RainA
  RainS
  Light
  1Wire
  WindS
  WindD
  Heat
  I2C
  3.3V

custom parts:
  SBX DSUN: SBX DSUN input voltage 4.5 - 28V DC output voltage .8v to 20VDC (step down converter) Output current 3A max
  ESP32 DevKitc V4: ESP32-DevKitC board with ESP32-WROOM-32 module. ESP32-DevKitC V4 is a small-sized ESP32-based development board produced by Espressif. Most of the pins on the ESP module are broken out to the pin headers on the board. The pins D0, D1, D2, D3, CMD and CLK are used internally for communication between ESP32 and SPI flash memory. They are grouped on both sides near the USB connector. Avoid using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
  Adafruit ADS1115 16Bit I2C ADC: For microcontrollers without an analog-to-digital converter or when you want a higher-precision ADC, the ADS1115 provides 16-bit precision at 860 samples/second over I2C. The chip can be configured as 4 single-ended input channels, or two differential channels. As a nice bonus, it even includes a programmable gain amplifier, up to x16, to help boost up smaller single/differential signals to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
