# Fritzing sketch weatherlox-temp-pcb (saved by Fritzing 1.0.6)
circuit board: 2.5cm x 3cm

parts:
  BME280 = GY-BMP280 Breakout
  Temp2 = screw terminal, 2 pins
  Temp1 = screw terminal, 2 pins

nets:
  N1: BME280.Pin_1, Temp1.pin1
  N2: BME280.Pin_2, Temp1.pin2
  N3: BME280.Pin_3, Temp2.pin2
  N4: BME280.Pin_4, Temp2.pin1

notes:
  (c) Michael Schlenstedt
  Version 1.00
  WeatherLox
